# Fritzing sketch Untitled Sketch (saved by Fritzing 0.9.3b)

parts:
  M1 = JSN-SRO4T [package=THT]
  esp1 = ESP32 DevKitc V4
  OLED_I2C1 = OLED 128x64 I2C Monochrome Display

nets:
  N1: M1.pin1, esp1.GND#32
  N2: M1.pin2, esp1.IO14
  N3: M1.pin3, esp1.IO27
  5V: M1.pin4, esp1.5V, OLED_I2C1.VDD
  N4: esp1.IO21, OLED_I2C1.SDA
  N5: esp1.IO22, OLED_I2C1.SCK
  N6: esp1.GND#18, OLED_I2C1.GND

custom parts:
  JSN-SRO4T: JSN-SR04T Waterproof Ultrasonic Distance Measuring Module Integrated Ultrasonic Detection Module DC 5V.
  ESP32 DevKitc V4: ESP32-DevKitC board with ESP32-WROOM-32 module. ESP32-DevKitC V4 is a small-sized ESP32-based development board produced by Espressif. Most of the pins on the ESP module are broken out to the pin headers on the board. The pins D0, D1, D2, D3, CMD and CLK are used internally for communication between ESP32 and SPI flash memory. They are grouped on both sides near the USB connector. Avoid using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
